// Logisim project main.circ as structural Verilog: 26 circuits, main circuit main
module main (
  input  enable,
  input  [63:0] in_data,
  input  [63:0] key,
  input  mode,
  output [63:0] out_data
);

  BlowfishCodec blowfishcodec_1 (.enable(enable), .in_data(in_data), .key(key), .mode(mode), .out_data(out_data));
endmodule

module BlowfishCodec (
  input  enable,
  input  [63:0] in_data,
  input  [63:0] key,
  input  mode,
  output [63:0] out_data
);

  wire not_1_out;
  wire [31:0] iteration_0_result_0, iteration_0_result_1, iteration_1_result_0, iteration_1_result_1,
       iteration_2_result_0, iteration_2_result_1, iteration_3_result_0, iteration_3_result_1,
       iteration_4_result_0, iteration_4_result_1, iteration_5_result_0, iteration_5_result_1,
       iteration_6_result_0, iteration_6_result_1, iteration_7_result_0, iteration_7_result_1,
       iteration_8_result_0, iteration_8_result_1, iteration_9_result_0, iteration_9_result_1,
       iteration_10_result_0, iteration_10_result_1, iteration_11_result_0, iteration_11_result_1,
       iteration_12_result_0, iteration_12_result_1, iteration_13_result_0, iteration_13_result_1,
       iteration_14_result_0, iteration_14_result_1, iteration_15_result_0, iteration_15_result_1,
       pblocks_1_out_3, pblocks_2_out_3, xor_1_out, xor_2_out;

  Iteration iteration_0 (
    .value_0(in_data[31:0]), .value_1(in_data[63:32]), .index({5{1'b0}}), .inverse(mode),
    .result_0(iteration_0_result_0), .result_1(iteration_0_result_1));
  Iteration iteration_1 (
    .value_0(iteration_0_result_0), .value_1(iteration_0_result_1), .index(5'b00001), .inverse(mode),
    .result_0(iteration_1_result_0), .result_1(iteration_1_result_1));
  Iteration iteration_2 (
    .value_0(iteration_1_result_0), .value_1(iteration_1_result_1), .index(5'b00010), .inverse(mode),
    .result_0(iteration_2_result_0), .result_1(iteration_2_result_1));
  Iteration iteration_3 (
    .value_0(iteration_2_result_0), .value_1(iteration_2_result_1), .index(5'b00011), .inverse(mode),
    .result_0(iteration_3_result_0), .result_1(iteration_3_result_1));
  Iteration iteration_4 (
    .value_0(iteration_3_result_0), .value_1(iteration_3_result_1), .index(5'b00100), .inverse(mode),
    .result_0(iteration_4_result_0), .result_1(iteration_4_result_1));
  Iteration iteration_5 (
    .value_0(iteration_4_result_0), .value_1(iteration_4_result_1), .index(5'b00101), .inverse(mode),
    .result_0(iteration_5_result_0), .result_1(iteration_5_result_1));
  Iteration iteration_6 (
    .value_0(iteration_5_result_0), .value_1(iteration_5_result_1), .index(5'b00110), .inverse(mode),
    .result_0(iteration_6_result_0), .result_1(iteration_6_result_1));
  Iteration iteration_7 (
    .value_0(iteration_6_result_0), .value_1(iteration_6_result_1), .index(5'b00111), .inverse(mode),
    .result_0(iteration_7_result_0), .result_1(iteration_7_result_1));
  Iteration iteration_8 (
    .value_0(iteration_7_result_0), .value_1(iteration_7_result_1), .index(5'b01000), .inverse(mode),
    .result_0(iteration_8_result_0), .result_1(iteration_8_result_1));
  Iteration iteration_9 (
    .value_0(iteration_8_result_0), .value_1(iteration_8_result_1), .index(5'b01001), .inverse(mode),
    .result_0(iteration_9_result_0), .result_1(iteration_9_result_1));
  Iteration iteration_10 (
    .value_0(iteration_9_result_0), .value_1(iteration_9_result_1), .index(5'b01010), .inverse(mode),
    .result_0(iteration_10_result_0), .result_1(iteration_10_result_1));
  Iteration iteration_11 (
    .value_0(iteration_10_result_0), .value_1(iteration_10_result_1), .index(5'b01011), .inverse(mode),
    .result_0(iteration_11_result_0), .result_1(iteration_11_result_1));
  Iteration iteration_12 (
    .value_0(iteration_11_result_0), .value_1(iteration_11_result_1), .index(5'b01100), .inverse(mode),
    .result_0(iteration_12_result_0), .result_1(iteration_12_result_1));
  Iteration iteration_13 (
    .value_0(iteration_12_result_0), .value_1(iteration_12_result_1), .index(5'b01101), .inverse(mode),
    .result_0(iteration_13_result_0), .result_1(iteration_13_result_1));
  Iteration iteration_14 (
    .value_0(iteration_13_result_0), .value_1(iteration_13_result_1), .index(5'b01110), .inverse(mode),
    .result_0(iteration_14_result_0), .result_1(iteration_14_result_1));
  Iteration iteration_15 (
    .value_0(iteration_14_result_0), .value_1(iteration_14_result_1), .index(5'b01111), .inverse(mode),
    .result_0(iteration_15_result_0), .result_1(iteration_15_result_1));
  assign xor_1_out = iteration_15_result_0 ^ pblocks_1_out_3;  // XOR_Gate xor_1, 32 bits wide
  PBlocks pblocks_1 (.index(5'b10001), .inverse(mode), .out_3(pblocks_1_out_3));
  assign xor_2_out = iteration_15_result_1 ^ pblocks_2_out_3;  // XOR_Gate xor_2, 32 bits wide
  PBlocks pblocks_2 (.index(5'b10000), .inverse(mode), .out_3(pblocks_2_out_3));
  not not_1 (not_1_out, enable);
  // Transmission_Gate #(.width(64)) transmission_1: pin names not known; wires that end beside it: {xor_1_out, xor_2_out}, not_1_out, enable, out_data
endmodule

module BitExtender1To32 (
  input  value,
  output [31:0] result
);


  assign result = {32{value}};
endmodule

module Multiplexer2 (
  input  [31:0] value_0,
  input  [31:0] value_1,
  input  choice,
  output [31:0] result
);

  wire [31:0] and_1_out, and_2_out, bitextender1to32_1_result, not_1_out;

  BitExtender1To32 bitextender1to32_1 (.value(choice), .result(bitextender1to32_1_result));
  assign not_1_out = ~bitextender1to32_1_result;  // NOT_Gate not_1, 32 bits wide
  assign and_1_out = value_0 & not_1_out;  // AND_Gate and_1, 32 bits wide
  assign result = and_1_out | and_2_out;  // OR_Gate or_1, 32 bits wide
  assign and_2_out = value_1 & bitextender1to32_1_result;  // AND_Gate and_2, 32 bits wide
endmodule

module Multiplexer4 (
  input  [31:0] value_0,
  input  [31:0] value_1,
  input  [31:0] value_2,
  input  [31:0] value_3,
  input  [1:0] choice,
  output [31:0] result
);

  wire [31:0] and_1_out, and_2_out, bitextender1to32_1_result, multiplexer2_1_result, multiplexer2_2_result,
       not_1_out;

  Multiplexer2 multiplexer2_1 (
    .value_0(value_0), .value_1(value_1), .choice(choice[0]), .result(multiplexer2_1_result));
  assign not_1_out = ~bitextender1to32_1_result;  // NOT_Gate not_1, 32 bits wide
  Multiplexer2 multiplexer2_2 (
    .value_0(value_2), .value_1(value_3), .choice(choice[0]), .result(multiplexer2_2_result));
  BitExtender1To32 bitextender1to32_1 (.value(choice[1]), .result(bitextender1to32_1_result));
  assign and_1_out = multiplexer2_1_result & not_1_out;  // AND_Gate and_1, 32 bits wide
  assign and_2_out = multiplexer2_2_result & bitextender1to32_1_result;  // AND_Gate and_2, 32 bits wide
  assign result = and_1_out | and_2_out;  // OR_Gate or_1, 32 bits wide
endmodule

module Multiplexer8 (
  input  [31:0] value_0,
  input  [31:0] value_1,
  input  [31:0] value_2,
  input  [31:0] value_3,
  input  [31:0] value_4,
  input  [31:0] value_5,
  input  [31:0] value_6,
  input  [31:0] value_7,
  input  [2:0] choice,
  output [31:0] result
);

  wire [31:0] and_1_out, and_2_out, bitextender1to32_1_result, multiplexer4_1_result, multiplexer4_2_result,
       not_1_out;

  Multiplexer4 multiplexer4_1 (
    .value_0(value_0), .value_1(value_1), .value_2(value_2), .value_3(value_3), .choice(choice[1:0]),
    .result(multiplexer4_1_result));
  assign not_1_out = ~bitextender1to32_1_result;  // NOT_Gate not_1, 32 bits wide
  Multiplexer4 multiplexer4_2 (
    .value_0(value_4), .value_1(value_5), .value_2(value_6), .value_3(value_7), .choice(choice[1:0]),
    .result(multiplexer4_2_result));
  BitExtender1To32 bitextender1to32_1 (.value(choice[2]), .result(bitextender1to32_1_result));
  assign and_1_out = multiplexer4_1_result & not_1_out;  // AND_Gate and_1, 32 bits wide
  assign and_2_out = multiplexer4_2_result & bitextender1to32_1_result;  // AND_Gate and_2, 32 bits wide
  assign result = and_1_out | and_2_out;  // OR_Gate or_1, 32 bits wide
endmodule

module Multiplexer16 (
  input  [31:0] value_0,
  input  [31:0] value_1,
  input  [31:0] value_2,
  input  [31:0] value_3,
  input  [31:0] value_4,
  input  [31:0] value_5,
  input  [31:0] value_6,
  input  [31:0] value_7,
  input  [31:0] value_8,
  input  [31:0] value_9,
  input  [31:0] value_10,
  input  [31:0] value_11,
  input  [31:0] value_12,
  input  [31:0] value_13,
  input  [31:0] value_14,
  input  [31:0] value_15,
  input  [3:0] choice,
  output [31:0] result
);

  wire [31:0] and_1_out, and_2_out, bitextender1to32_1_result, multiplexer8_1_result, multiplexer8_2_result,
       not_1_out;

  Multiplexer8 multiplexer8_1 (
    .value_0(value_0), .value_1(value_1), .value_2(value_2), .value_3(value_3), .value_4(value_4),
    .value_5(value_5), .value_6(value_6), .value_7(value_7), .choice(choice[2:0]),
    .result(multiplexer8_1_result));
  assign not_1_out = ~bitextender1to32_1_result;  // NOT_Gate not_1, 32 bits wide
  Multiplexer8 multiplexer8_2 (
    .value_0(value_8), .value_1(value_9), .value_2(value_10), .value_3(value_11), .value_4(value_12),
    .value_5(value_13), .value_6(value_14), .value_7(value_15), .choice(choice[2:0]),
    .result(multiplexer8_2_result));
  BitExtender1To32 bitextender1to32_1 (.value(choice[3]), .result(bitextender1to32_1_result));
  assign and_1_out = multiplexer8_1_result & not_1_out;  // AND_Gate and_1, 32 bits wide
  assign and_2_out = multiplexer8_2_result & bitextender1to32_1_result;  // AND_Gate and_2, 32 bits wide
  assign result = and_1_out | and_2_out;  // OR_Gate or_1, 32 bits wide
endmodule

module Multiplexer32 (
  input  [31:0] value_0,
  input  [31:0] value_1,
  input  [31:0] value_2,
  input  [31:0] value_3,
  input  [31:0] value_4,
  input  [31:0] value_5,
  input  [31:0] value_6,
  input  [31:0] value_7,
  input  [31:0] value_8,
  input  [31:0] value_9,
  input  [31:0] value_10,
  input  [31:0] value_11,
  input  [31:0] value_12,
  input  [31:0] value_13,
  input  [31:0] value_14,
  input  [31:0] value_15,
  input  [31:0] value_16,
  input  [31:0] value_17,
  input  [31:0] value_18,
  input  [31:0] value_19,
  input  [31:0] value_20,
  input  [31:0] value_21,
  input  [31:0] value_22,
  input  [31:0] value_23,
  input  [31:0] value_24,
  input  [31:0] value_25,
  input  [31:0] value_26,
  input  [31:0] value_27,
  input  [31:0] value_28,
  input  [31:0] value_29,
  input  [31:0] value_30,
  input  [31:0] value_31,
  input  [4:0] choice,
  output [31:0] out_34
);

  wire [31:0] and_1_out, and_2_out, bitextender1to32_1_result, multiplexer16_1_result,
       multiplexer16_2_result, not_1_out;

  Multiplexer16 multiplexer16_1 (
    .value_0(value_0), .value_1(value_1), .value_2(value_2), .value_3(value_3), .value_4(value_4),
    .value_5(value_5), .value_6(value_6), .value_7(value_7), .value_8(value_8), .value_9(value_9),
    .value_10(value_10), .value_11(value_11), .value_12(value_12), .value_13(value_13), .value_14(value_14),
    .value_15(value_15), .choice(choice[3:0]), .result(multiplexer16_1_result));
  Multiplexer16 multiplexer16_2 (
    .value_0(value_16), .value_1(value_17), .value_2(value_18), .value_3(value_19), .value_4(value_20),
    .value_5(value_21), .value_6(value_22), .value_7(value_23), .value_8(value_24), .value_9(value_25),
    .value_10(value_26), .value_11(value_27), .value_12(value_28), .value_13(value_29), .value_14(value_30),
    .value_15(value_31), .choice(choice[3:0]), .result(multiplexer16_2_result));
  BitExtender1To32 bitextender1to32_1 (.value(choice[4]), .result(bitextender1to32_1_result));
  assign and_1_out = multiplexer16_1_result & not_1_out;  // AND_Gate and_1, 32 bits wide
  assign not_1_out = ~bitextender1to32_1_result;  // NOT_Gate not_1, 32 bits wide
  assign and_2_out = multiplexer16_2_result & bitextender1to32_1_result;  // AND_Gate and_2, 32 bits wide
  assign out_34 = and_1_out | and_2_out;  // OR_Gate or_1, 32 bits wide
endmodule

module FFunction (
  input  [31:0] value,
  output [31:0] out_2
);

  wire [31:0] adder_1_result, sbox0_1_result, sbox1_1_result, sbox2_1_result, sbox3_1_result, xor_1_out;

  SBox0 sbox0_1 (.in_data(value[31:24]), .result(sbox0_1_result));
  SBox1 sbox1_1 (.in_data(value[23:16]), .result(sbox1_1_result));
  SBox2 sbox2_1 (.in_data(value[15:8]), .result(sbox2_1_result));
  SBox3 sbox3_1 (.in_data(value[7:0]), .result(sbox3_1_result));
  Adder adder_1 (.value_0(sbox0_1_result), .value_1(sbox1_1_result), .result(adder_1_result));
  assign xor_1_out = adder_1_result ^ sbox2_1_result;  // XOR_Gate xor_1, 32 bits wide
  Adder adder_2 (.value_0(sbox3_1_result), .value_1(xor_1_out), .result(out_2));
endmodule

module SBox0 (
  input  [7:0] in_data,
  output [31:0] result
);

  Multiplexer #(.disabled("Z"), .select(8), .width(32)) multiplexer_1 (
    .in0(32'h1b63c83d), .in1(32'h748297fe), .in2(32'hb92e77a), .in3(32'ha5530603), .in4(32'he50691ca),
    .in5(32'he63d8bfb), .in6(32'h4777d9b6), .in7(32'ha5bbb7f9), .in8(32'h2169ad09), .in9(32'h15fee6e),
    .in10(32'h45c63eba), .in11(32'h9a1ecb32), .in12(32'hd07b3183), .in13(32'hd52860f), .in14(32'h10ad564f),
    .in15(32'ha6162dc9), .in16(32'hc80ab49a), .in17(32'hefeb5c56), .in18(32'heefc7386), .in19(32'h415fd936),
    .in20(32'he2612b88), .in21(32'h5a9d7a9d), .in22(32'h1a66e785), .in23(32'h1e5880df), .in24(32'h4f662e72),
    .in25(32'h8cbc668c), .in26(32'ha32f4d86), .in27(32'h8ffa6138), .in28(32'h5740c414), .in29(32'hb30d4cac),
    .in30(32'h74e7eb4d), .in31(32'he1c00d30), .in32(32'hc41b3a1c), .in33(32'h5d5d3ed4), .in34(32'hd4da660a),
    .in35(32'h4c722295), .in36(32'ha0e14b63), .in37(32'h9229b90a), .in38(32'h6ca3b48a), .in39(32'hb36d26a),
    .in40(32'h72f390d2), .in41(32'h3a781ac9), .in42(32'hc5a9c3c9), .in43(32'h2a1af33b), .in44(32'h2c2f34f3),
    .in45(32'h25eaefbe), .in46(32'hbc10f2dd), .in47(32'h76b2242e), .in48(32'hce7a095d), .in49(32'hb5d8ac5c),
    .in50(32'haa5f303f), .in51(32'h57579120), .in52(32'hb0867e52), .in53(32'he9538045), .in54(32'h59c80b57),
    .in55(32'h4b07ee7b), .in56(32'hfe2e3c1a), .in57(32'h514e312b), .in58(32'hbf36d761), .in59(32'hebdcb659),
    .in60(32'h49939dff), .in61(32'h9cb92877), .in62(32'hcbcb78a6), .in63(32'h76ca0fb2), .in64(32'h239e55e2),
    .in65(32'h4e9f60ae), .in66(32'hd446d310), .in67(32'hc7a4d6a9), .in68(32'hb2b2608c), .in69(32'h393f64d0),
    .in70(32'h799506c2), .in71(32'he0ed153e), .in72(32'hbedc6611), .in73(32'hc07cacce), .in74(32'hd5facbe),
    .in75(32'h36c6bb30), .in76(32'hdc7a3890), .in77(32'hfa39840), .in78(32'hd19157b4), .in79(32'h99aeec25),
    .in80(32'hd2eff09a), .in81(32'h64d8f1ad), .in82(32'h625e6b41), .in83(32'hfb8eaa2e), .in84(32'hedeab89d),
    .in85(32'h2a8846db), .in86(32'h3da74bfb), .in87(32'hec0fc13c), .in88(32'h94d374d1), .in89(32'h50b937cc),
    .in90(32'h396c2e0e), .in91(32'h14290663), .in92(32'h69c291a2), .in93(32'hc0a1f8d3), .in94(32'h1e618183),
    .in95(32'hd0f79fdd), .in96(32'h2382017e), .in97(32'h14dcc723), .in98(32'hab944fad), .in99(32'h11b484bc),
    .in100(32'h9c9236ff), .in101(32'h2fd8ee44), .in102(32'h7c85b7f8), .in103(32'h7207f167),
    .in104(32'h26ba6278), .in105(32'h9b36e2f), .in106(32'he954d6b4), .in107(32'hca37ff2),
    .in108(32'ha835b6ca), .in109(32'h71d5b7f9), .in110(32'h7a5846f6), .in111(32'he36c9ff1),
    .in112(32'heb1aa1df), .in113(32'h7f76f059), .in114(32'hd8645427), .in115(32'h19b2e3b1),
    .in116(32'hcb3819ab), .in117(32'h6cdd4583), .in118(32'h3fb9dd25), .in119(32'h3fc0566a),
    .in120(32'h23140233), .in121(32'h232e5d02), .in122(32'h70f1c72e), .in123(32'h8d060237),
    .in124(32'hba732309), .in125(32'h5c93cc8a), .in126(32'h4a430611), .in127(32'h2e0f49c8),
    .in128(32'hb0280eae), .in129(32'h8c059404), .in130(32'h5a17008c), .in131(32'hbfd3b756),
    .in132(32'h660b8acd), .in133(32'h91c7aff6), .in134(32'h6e4a34b3), .in135(32'h288f1d0c),
    .in136(32'hbc0a2a8), .in137(32'ha12aced0), .in138(32'hc664e60b), .in139(32'h7732b348),
    .in140(32'h6e05e400), .in141(32'h627d8b29), .in142(32'he2ac6f6f), .in143(32'h406d2355),
    .in144(32'hf1712267), .in145(32'hcbd9042f), .in146(32'hd9377910), .in147(32'h1aadd572),
    .in148(32'h363276af), .in149(32'hd6af54c6), .in150(32'haf9c601e), .in151(32'h2343f30c),
    .in152(32'h9b77c4d3), .in153(32'h3635bbc3), .in154(32'h3574a04b), .in155(32'heed33285),
    .in156(32'h38209b78), .in157(32'h2d33ffe2), .in158(32'h8994d7e9), .in159(32'he9d7b20c),
    .in160(32'h926f310), .in161(32'h92c1e5c2), .in162(32'h53b56f75), .in163(32'h18153a43),
    .in164(32'hc432bff9), .in165(32'ha2e11d9), .in166(32'h82619ace), .in167(32'h7260d846),
    .in168(32'h11960521), .in169(32'h247f342d), .in170(32'h9d1000b), .in171(32'h6cae1ae7),
    .in172(32'h1a2c61e6), .in173(32'h424e2a9a), .in174(32'he2bfc9df), .in175(32'h84e1a0a8),
    .in176(32'h520db870), .in177(32'h37f17dbc), .in178(32'h4c7dbcc0), .in179(32'hfe7316da),
    .in180(32'h55e726f6), .in181(32'h92392795), .in182(32'h6299370a), .in183(32'ha28466ab),
    .in184(32'hbccd6504), .in185(32'h6f58dc1f), .in186(32'h40c8b9df), .in187(32'h7c1da11f),
    .in188(32'h191ac154), .in189(32'hde9ca86b), .in190(32'h942e29ab), .in191(32'hc76c5ea4),
    .in192(32'h3aa475aa), .in193(32'h986a653), .in194(32'h3be45d3f), .in195(32'h69463e11),
    .in196(32'h19c917b4), .in197(32'h208ca1df), .in198(32'h5dad641a), .in199(32'h5ac42e52),
    .in200(32'h7fa31dd3), .in201(32'h76a82c6), .in202(32'hf2508876), .in203(32'h2c4a92fc),
    .in204(32'ha96773cc), .in205(32'h2a01eefc), .in206(32'hc34c054e), .in207(32'hc6e90f44),
    .in208(32'he73c9b11), .in209(32'hfd978763), .in210(32'ha649ecc1), .in211(32'h1679bb12),
    .in212(32'h86118cb3), .in213(32'h9734cc11), .in214(32'h3d016159), .in215(32'hb4f293eb),
    .in216(32'hc71582c9), .in217(32'hd72d2109), .in218(32'hdf51eb41), .in219(32'h5cb7deaa),
    .in220(32'h95746ec8), .in221(32'h1c85facc), .in222(32'h3a618cde), .in223(32'h6ab3db91),
    .in224(32'h5e159fe6), .in225(32'h7132486b), .in226(32'h8073fd18), .in227(32'h865cc729),
    .in228(32'h9dce0bb8), .in229(32'h23be152d), .in230(32'hc097918e), .in231(32'h3f60b9d6),
    .in232(32'hdea35bc2), .in233(32'hfec94e70), .in234(32'hbb064d28), .in235(32'hf6ddf1c2),
    .in236(32'h4234ed8d), .in237(32'h76e5cd04), .in238(32'h78ce76c9), .in239(32'h97cded43),
    .in240(32'h706d2108), .in241(32'h5f79df83), .in242(32'h6a3723c5), .in243(32'hb277ee6b),
    .in244(32'h38a36bd2), .in245(32'h1f8228c3), .in246(32'h1a754f50), .in247(32'h31f0b164),
    .in248(32'he14c1f50), .in249(32'ha1a781f5), .in250(32'hf67c2ac1), .in251(32'heefb4162),
    .in252(32'hb9adb3c6), .in253(32'hae225666), .in254(32'h97df1836), .in255(32'h19683659), .out(result),
    .sel(in_data));
endmodule

module SBox1 (
  input  [7:0] in_data,
  output [31:0] result
);

  Multiplexer #(.disabled("Z"), .select(8), .width(32)) multiplexer_1 (
    .in0(32'h4d6e67c7), .in1(32'hf0b07072), .in2(32'h9e042e51), .in3(32'h508dfd5f), .in4(32'h1bcb2115),
    .in5(32'h5b63c172), .in6(32'hd3a2f85b), .in7(32'h868f9927), .in8(32'ha3680d51), .in9(32'hc5b6fbfb),
    .in10(32'haf018afb), .in11(32'h49866c45), .in12(32'hdfeb30c5), .in13(32'hfc9ae25a), .in14(32'h21ae6dfe),
    .in15(32'had2efa53), .in16(32'h9a271177), .in17(32'hfd0da6dd), .in18(32'h7506caa0), .in19(32'h125a0ae5),
    .in20(32'h46e9aa07), .in21(32'h1a40cff4), .in22(32'h1d775a26), .in23(32'hb88cbc26), .in24(32'h37640cc6),
    .in25(32'hb1f668db), .in26(32'he9c89e11), .in27(32'hd2798956), .in28(32'h8f1fd8ce), .in29(32'hebc569ff),
    .in30(32'h956d876c), .in31(32'h7e197efd), .in32(32'hc2ebc5b6), .in33(32'hb120eb7a), .in34(32'h5fad20c8),
    .in35(32'h35cfd4af), .in36(32'hb2fe0cec), .in37(32'h8773a6ab), .in38(32'h50f855ea), .in39(32'hada1b083),
    .in40(32'ha54f714), .in41(32'h23f7233f), .in42(32'h34520090), .in43(32'hbafe785a), .in44(32'h8e86a108),
    .in45(32'hd83ee0dc), .in46(32'h1d795f19), .in47(32'hed9bd661), .in48(32'hc583c77), .in49(32'hfdeff89e),
    .in50(32'h68fa0486), .in51(32'h55a8dd56), .in52(32'h6d3b5a04), .in53(32'h54624129), .in54(32'hfd4a23ae),
    .in55(32'hbd0a0bc6), .in56(32'h6d623b56), .in57(32'h4724a899), .in58(32'hf2c4ac82), .in59(32'he65e86fb),
    .in60(32'h3cdb3da3), .in61(32'h950dbbc7), .in62(32'h1dd1aef6), .in63(32'hc09d456d), .in64(32'hdda357bf),
    .in65(32'hcb2d08d4), .in66(32'h3a477f05), .in67(32'h7080354e), .in68(32'haa8f3a58), .in69(32'hfd86e4bd),
    .in70(32'he0a63e94), .in71(32'h54743cc7), .in72(32'h2510e924), .in73(32'he8ff6700), .in74(32'h34c4c7ba),
    .in75(32'h4287dbba), .in76(32'hbaed9fcb), .in77(32'hece8004f), .in78(32'haaa57523), .in79(32'h85d3e2dd),
    .in80(32'h8bfd2a53), .in81(32'h487e6f86), .in82(32'h5ef4339d), .in83(32'h4c7e2bd1), .in84(32'hc3265daf),
    .in85(32'hc12c6cf5), .in86(32'h7c3ef837), .in87(32'h61d23728), .in88(32'h4e1f35b0), .in89(32'h9edf487f),
    .in90(32'hcf60ec9b), .in91(32'h43e4d5aa), .in92(32'hd9ed3bfc), .in93(32'hdf88169e), .in94(32'hb69f01d8),
    .in95(32'h465b6018), .in96(32'h7e8c3588), .in97(32'h1cb45420), .in98(32'hb1aead40), .in99(32'h99e2f6),
    .in100(32'h87e377f8), .in101(32'ha451aa4c), .in102(32'h7e80d65a), .in103(32'h7ec46ee3),
    .in104(32'h8d0253f4), .in105(32'ha8d940e9), .in106(32'h7e6aaff7), .in107(32'hdafadd10),
    .in108(32'hb3a99cd1), .in109(32'h109b2842), .in110(32'hd0adaa33), .in111(32'habe75824),
    .in112(32'h2af0cbb0), .in113(32'h8d13fc6f), .in114(32'h1516e5e4), .in115(32'h9d03a8d9),
    .in116(32'hc5cb257), .in117(32'h2208ed62), .in118(32'hf735f380), .in119(32'h26ab700a),
    .in120(32'h431c87ac), .in121(32'h2097b723), .in122(32'h36d4cdac), .in123(32'h4f5bb432),
    .in124(32'h9a7f4fe5), .in125(32'h71fa6910), .in126(32'h25e0a910), .in127(32'h2a57f80f),
    .in128(32'h5b5bad76), .in129(32'h965b9808), .in130(32'hd116a32), .in131(32'h5ecf1111),
    .in132(32'h68ce7fd6), .in133(32'ha59005f2), .in134(32'h78b8a7c2), .in135(32'h28599440),
    .in136(32'hcc76ae6a), .in137(32'ha19848c0), .in138(32'h473475ed), .in139(32'hf381f26b),
    .in140(32'h809508a6), .in141(32'h7a1ca233), .in142(32'hfd3e8320), .in143(32'h43644bdd),
    .in144(32'h8575316b), .in145(32'h2dc8d72c), .in146(32'hb4db59af), .in147(32'h192d959b),
    .in148(32'h9f16b2ea), .in149(32'h67ba02f8), .in150(32'h776d7d3f), .in151(32'h3f6ecf9e),
    .in152(32'h5d474ee5), .in153(32'hf93e1b5), .in154(32'h10e5b1a7), .in155(32'h464f8d2),
    .in156(32'h7b862a2b), .in157(32'h8f350fdd), .in158(32'h1e8f90ac), .in159(32'he9199f7c),
    .in160(32'h456e5675), .in161(32'h1832ffc1), .in162(32'hf2fe9222), .in163(32'h468b0b98),
    .in164(32'h20ecce95), .in165(32'ha992685f), .in166(32'hd650677e), .in167(32'hfc8a429a),
    .in168(32'hf0cec9af), .in169(32'h957a695f), .in170(32'h7c6613b2), .in171(32'h175f0cc8),
    .in172(32'ha02149f3), .in173(32'h278f57b7), .in174(32'h8ff16cd8), .in175(32'h53d3e8c6),
    .in176(32'hadc47cd9), .in177(32'hb69f7aee), .in178(32'h7d3adb5f), .in179(32'hfdf45193),
    .in180(32'h87f8b90c), .in181(32'ha984c74c), .in182(32'hb328f23e), .in183(32'ha7575fe4),
    .in184(32'hf3acecc2), .in185(32'h5dd0af7f), .in186(32'h279bd213), .in187(32'h13498e61),
    .in188(32'h4939d133), .in189(32'h74ea4d26), .in190(32'h17e17db), .in191(32'h39ec8cae),
    .in192(32'h223a7186), .in193(32'hf42f85cb), .in194(32'h84701773), .in195(32'h9949a914),
    .in196(32'h7f8b2e0b), .in197(32'hfb4a6b2d), .in198(32'hbe510c47), .in199(32'h598ecd03),
    .in200(32'h8d5d1cd1), .in201(32'hd261937c), .in202(32'h889d2202), .in203(32'had75216b),
    .in204(32'h3110128e), .in205(32'h80cf5859), .in206(32'he5dad1), .in207(32'h53908942),
    .in208(32'h622f9094), .in209(32'h7be310c), .in210(32'ha14a6969), .in211(32'h44c125cb),
    .in212(32'h1f43dfa1), .in213(32'h368c7993), .in214(32'h3ed95c2f), .in215(32'hb943e2a0),
    .in216(32'h96ae7d2a), .in217(32'h9e36dfa8), .in218(32'h93ece687), .in219(32'h46208cad),
    .in220(32'h482c6e8a), .in221(32'he5a0bee1), .in222(32'h71a60570), .in223(32'h55c73148),
    .in224(32'h47cdd000), .in225(32'h5c92cb55), .in226(32'heb0c30e6), .in227(32'h6b5dc999),
    .in228(32'h3ade1354), .in229(32'h6fee93d3), .in230(32'h742eaea1), .in231(32'h16174acc),
    .in232(32'h410ab682), .in233(32'hd2861806), .in234(32'h858c5db1), .in235(32'hf0be357f),
    .in236(32'h280ec210), .in237(32'ha5b9c2e8), .in238(32'hfb33cc3c), .in239(32'h1427c8a0),
    .in240(32'h1a7e7bd4), .in241(32'h5a9723d5), .in242(32'h78e8e7b0), .in243(32'hcdd2ab01),
    .in244(32'hd84f4350), .in245(32'hdc3846fc), .in246(32'h14d50cc4), .in247(32'h2ad12ce1),
    .in248(32'h4ca9aa9b), .in249(32'he21d7e71), .in250(32'h34f7a0df), .in251(32'h6190acfa),
    .in252(32'h23b14e55), .in253(32'ha64f9b2b), .in254(32'h61dae2b1), .in255(32'h2b974f87), .out(result),
    .sel(in_data));
endmodule

module SBox2 (
  input  [7:0] in_data,
  output [31:0] result
);

  Multiplexer #(.disabled("Z"), .select(8), .width(32)) multiplexer_1 (
    .in0(32'h92023346), .in1(32'h2d407324), .in2(32'he7facd16), .in3(32'h20e92ee1), .in4(32'h398e4c4d),
    .in5(32'h475f65f4), .in6(32'h8ce0f32b), .in7(32'h134e59ea), .in8(32'h5c15f87a), .in9(32'h26b05e2e),
    .in10(32'h2b9767dc), .in11(32'h8dcc716b), .in12(32'h49538a9f), .in13(32'h1e0575a2), .in14(32'hbfc4038),
    .in15(32'hd500ecca), .in16(32'h453bccc9), .in17(32'heae47e6), .in18(32'h18488d00), .in19(32'ha61039a5),
    .in20(32'hf436d5a9), .in21(32'h82fb702f), .in22(32'h81b3a290), .in23(32'hcc72c9d9), .in24(32'he3a56b0),
    .in25(32'he977c742), .in26(32'h4dd3752c), .in27(32'h8ae17fa9), .in28(32'h1c1542a4), .in29(32'h12f7b2a8),
    .in30(32'h8097e6ab), .in31(32'h8bd53edf), .in32(32'hcb707b5b), .in33(32'h61a799d8), .in34(32'h1b927a27),
    .in35(32'hd3d10fb5), .in36(32'hf69b9c98), .in37(32'h24805135), .in38(32'h70a14b8), .in39(32'h5742fdb4),
    .in40(32'h1b436b5d), .in41(32'h9eda36e3), .in42(32'hc1117fda), .in43(32'ha0af548d), .in44(32'h29a24d0),
    .in45(32'hdf594f5a), .in46(32'hcefac026), .in47(32'h60f34b87), .in48(32'hba38b55d), .in49(32'he1e72a7d),
    .in50(32'h46eff571), .in51(32'hfc6f2f9c), .in52(32'h1aa74fa1), .in53(32'he4e6149b), .in54(32'h69e57894),
    .in55(32'hd42c8ebb), .in56(32'h8b7ea6d1), .in57(32'h26b8ed1a), .in58(32'hb579a8c0), .in59(32'h860fe069),
    .in60(32'hf8fb74ac), .in61(32'h7a877fa9), .in62(32'hd9f6deb4), .in63(32'h572ef89b), .in64(32'h580835ce),
    .in65(32'h376ed61a), .in66(32'h2941b0d7), .in67(32'he431c87d), .in68(32'hc5dcba8b), .in69(32'hf00fd9fb),
    .in70(32'h8e13ecdb), .in71(32'ha2c1ac2d), .in72(32'h7a1d6a02), .in73(32'hd44926da), .in74(32'hc06ce3d0),
    .in75(32'hcb9d3d0f), .in76(32'h3b0cc64a), .in77(32'h8ab5cf), .in78(32'hfd68d3e8), .in79(32'hada00e68),
    .in80(32'h574e24b8), .in81(32'hda4adc1f), .in82(32'h6221eb14), .in83(32'h6a1b3748), .in84(32'h9754f84a),
    .in85(32'h4e44bdec), .in86(32'hd86baf4f), .in87(32'hb52158c1), .in88(32'h9f73bf2c), .in89(32'hdd26ab0f),
    .in90(32'hf5ab4905), .in91(32'hc16d2e8), .in92(32'h8b3e8943), .in93(32'ha5327bd3), .in94(32'hf296949c),
    .in95(32'h1b4d8cf8), .in96(32'ha2ef1c77), .in97(32'hdb23df48), .in98(32'hdbe313e7), .in99(32'h366e5463),
    .in100(32'ha8d83ad6), .in101(32'hc6c0cc50), .in102(32'h237bda9a), .in103(32'h6220281a),
    .in104(32'h839937bc), .in105(32'hcf5fe4db), .in106(32'h354901b5), .in107(32'h23761500),
    .in108(32'hb915fcd5), .in109(32'hdef1f7ae), .in110(32'hc9eca1c9), .in111(32'hbcbb1f6c),
    .in112(32'h2f27c9f1), .in113(32'hb2d1a81f), .in114(32'h4da04fbf), .in115(32'hef3a4b18),
    .in116(32'h1438591f), .in117(32'h4cc8ca27), .in118(32'h53fe9512), .in119(32'h92a5089c),
    .in120(32'h16b2fcc5), .in121(32'h53fd14a), .in122(32'h5f122595), .in123(32'ha7b8dac1),
    .in124(32'h1b96bc46), .in125(32'h33c506a7), .in126(32'hccc33268), .in127(32'h3c30e05c),
    .in128(32'h8ee17db9), .in129(32'h8cb41ca3), .in130(32'h7b9cb24e), .in131(32'hf7ca53c2),
    .in132(32'h573de9bf), .in133(32'h4e3e5bb3), .in134(32'h41a82f79), .in135(32'he8692ddd),
    .in136(32'hf1057646), .in137(32'h5deae89), .in138(32'ha3915268), .in139(32'h701fc1a2),
    .in140(32'h473e120a), .in141(32'h6a4a7b4), .in142(32'h915dc87a), .in143(32'he8e95a2a),
    .in144(32'ha24ea9e2), .in145(32'h4658f446), .in146(32'h5f0cb382), .in147(32'h42cd424f),
    .in148(32'h6e3b99da), .in149(32'h98b9f28b), .in150(32'he119855e), .in151(32'h5e963c49),
    .in152(32'h3164624a), .in153(32'h4a2203f4), .in154(32'h405d5c3a), .in155(32'h421c81a4),
    .in156(32'h7bdd9bcb), .in157(32'h4a260bf2), .in158(32'h53b6f3cc), .in159(32'hac0c524a),
    .in160(32'h2fabfcb3), .in161(32'hf5aeb64e), .in162(32'haa6aaea), .in163(32'h2ab6e27a),
    .in164(32'h9751fbd8), .in165(32'h71d64e81), .in166(32'h4514fae5), .in167(32'h1ad3dd83),
    .in168(32'h4e457586), .in169(32'hb7fb8c63), .in170(32'h784e1132), .in171(32'h548ab0c3),
    .in172(32'h490e3ca9), .in173(32'h6946b6b5), .in174(32'hc5058592), .in175(32'h26fa87eb),
    .in176(32'ha346d731), .in177(32'hdda1de3b), .in178(32'h568c4b32), .in179(32'ha064eecd),
    .in180(32'hee67af05), .in181(32'h1cb934c0), .in182(32'hfbcb387f), .in183(32'h4ebf0db7),
    .in184(32'he0f7067f), .in185(32'hb771035), .in186(32'hc676fad7), .in187(32'ha02e8289),
    .in188(32'h92b0de65), .in189(32'h58b012ef), .in190(32'h96ddb161), .in191(32'h36ff552e),
    .in192(32'hef94f6f4), .in193(32'h7024e1ab), .in194(32'h1b180363), .in195(32'h3ea211a9),
    .in196(32'h80601494), .in197(32'h81b667b6), .in198(32'h281722cc), .in199(32'hfe41fd71),
    .in200(32'hb92541b9), .in201(32'h3abb8074), .in202(32'h78709b47), .in203(32'h7eaad350),
    .in204(32'h9d5c3379), .in205(32'h299a2815), .in206(32'hd22b4afd), .in207(32'hf7b7fa88),
    .in208(32'h72c07f01), .in209(32'h5e7b5d58), .in210(32'h928694ad), .in211(32'h1d374e6e),
    .in212(32'h491c97a0), .in213(32'h34dcc64a), .in214(32'h19ddef18), .in215(32'h3e7f7d2c),
    .in216(32'h12b43e43), .in217(32'h9268af9f), .in218(32'hb99e7da0), .in219(32'h7810de0f),
    .in220(32'h84ee6002), .in221(32'haa66cdbc), .in222(32'h3d3ce8db), .in223(32'h6ae9376e),
    .in224(32'hb6af3090), .in225(32'he3808d4d), .in226(32'h9691e892), .in227(32'h76b842b9),
    .in228(32'ha440bd11), .in229(32'h6fbba9aa), .in230(32'hd3ac963b), .in231(32'h95fec8be),
    .in232(32'h92da63b0), .in233(32'h19b97fb1), .in234(32'hf71fd002), .in235(32'h4880843b),
    .in236(32'h6170f00a), .in237(32'h9135d37c), .in238(32'h6e3b7fcb), .in239(32'h58ba7e1f),
    .in240(32'hed5353b5), .in241(32'haae591e1), .in242(32'h13e524c), .in243(32'heb63ab98),
    .in244(32'hf7547216), .in245(32'h1d70441a), .in246(32'hb6506516), .in247(32'hdd188a05),
    .in248(32'hf72e69ff), .in249(32'hd06c369b), .in250(32'h67a25b09), .in251(32'h93b547b),
    .in252(32'h6d88fa6c), .in253(32'h7ac0b224), .in254(32'h3c38c3dd), .in255(32'hff7dbfed), .out(result),
    .sel(in_data));
endmodule

module SBox3 (
  input  [7:0] in_data,
  output [31:0] result
);

  Multiplexer #(.disabled("Z"), .select(8), .width(32)) multiplexer_1 (
    .in0(32'h78939449), .in1(32'hc012af48), .in2(32'h53415ace), .in3(32'hfad9f6fe), .in4(32'h371e828a),
    .in5(32'h9eee04a8), .in6(32'h6960007a), .in7(32'h2884946c), .in8(32'h456e04f4), .in9(32'h7aed3cc9),
    .in10(32'hab3a36eb), .in11(32'h5683eab0), .in12(32'hfa7d68c), .in13(32'h5a85244d), .in14(32'he4d82152),
    .in15(32'h4103a7d3), .in16(32'hc5eac64c), .in17(32'hbc22702a), .in18(32'ha1d8f565), .in19(32'hca9a632f),
    .in20(32'hdc0ce79d), .in21(32'h885da03), .in22(32'h9be9e185), .in23(32'ha603aade), .in24(32'h7a6d0fac),
    .in25(32'heb1db30), .in26(32'h728d533a), .in27(32'h35277ee6), .in28(32'h1134bee7), .in29(32'hdb08d008),
    .in30(32'h5f926c20), .in31(32'h9115b6a7), .in32(32'h578ba049), .in33(32'h800f8952), .in34(32'h67a306ad),
    .in35(32'h693636b0), .in36(32'h714b1ce), .in37(32'h3992cf90), .in38(32'h7c7d3e61), .in39(32'hfc1a4),
    .in40(32'h55fda49d), .in41(32'h18861fe9), .in42(32'hae91095d), .in43(32'hdb4e7e3f), .in44(32'hd5b75b11),
    .in45(32'h46df12cf), .in46(32'h398240aa), .in47(32'h832546b0), .in48(32'h5ff1e329), .in49(32'h2c7fcf37),
    .in50(32'h75ccdd7a), .in51(32'h57f03f2b), .in52(32'h1864e9b6), .in53(32'h1d850ac7), .in54(32'hd607e4e7),
    .in55(32'heeb19970), .in56(32'hb1b3ffcc), .in57(32'hb29e5456), .in58(32'h8b29482b), .in59(32'h9674f9f0),
    .in60(32'h49da3baf), .in61(32'h23b9c936), .in62(32'hedfa6a7), .in63(32'hf08d94de), .in64(32'h737c0d21),
    .in65(32'hdbffc79f), .in66(32'h4ec419b0), .in67(32'hc71357e9), .in68(32'h16d08fee), .in69(32'he68e5d51),
    .in70(32'ha8659920), .in71(32'h92fa8600), .in72(32'h626acae1), .in73(32'hedfd8514), .in74(32'h8d4f1521),
    .in75(32'ha3661ee6), .in76(32'h1b1e31e7), .in77(32'h2a16acb), .in78(32'h879133f7), .in79(32'h83196d6),
    .in80(32'h737c5824), .in81(32'h42957cec), .in82(32'hb786dcb7), .in83(32'hcd4cea4e), .in84(32'he98be863),
    .in85(32'h3beface3), .in86(32'hb3d585d1), .in87(32'h92ba0891), .in88(32'h95e689f8), .in89(32'hf2044c02),
    .in90(32'h69aaaa16), .in91(32'ha9aa804a), .in92(32'hed4df94b), .in93(32'ha28f1e61), .in94(32'h69aebba),
    .in95(32'h40e8f4be), .in96(32'h84559444), .in97(32'h49214404), .in98(32'h35d78ce6), .in99(32'h1af7b5c4),
    .in100(32'h92887c85), .in101(32'h2d2b6453), .in102(32'hb294f172), .in103(32'h36cb37c8),
    .in104(32'h4955727c), .in105(32'h16cb3971), .in106(32'hdccc1cd6), .in107(32'h6dac7624),
    .in108(32'hc9386224), .in109(32'h2cd164bc), .in110(32'h5293d6dc), .in111(32'hdae6b916),
    .in112(32'ha2e90359), .in113(32'ha95a86d4), .in114(32'he5514c5c), .in115(32'h6d777962),
    .in116(32'hee33b952), .in117(32'hb8ab30a7), .in118(32'hada86efd), .in119(32'h47add9e2),
    .in120(32'h303953e8), .in121(32'h65dcc2bc), .in122(32'h611946a8), .in123(32'ha44f616f),
    .in124(32'ha6ece274), .in125(32'he4a52149), .in126(32'he6d5c1c2), .in127(32'h8774335d),
    .in128(32'h4347d9df), .in129(32'h9f2f8c1c), .in130(32'h909a93c6), .in131(32'hf80ec428),
    .in132(32'h96f77636), .in133(32'he91a58ba), .in134(32'heebd4890), .in135(32'ha232a75e),
    .in136(32'h823f6db0), .in137(32'h87f6f328), .in138(32'hb2dbcc8a), .in139(32'h86648214),
    .in140(32'hbb4bc47d), .in141(32'ha976c549), .in142(32'h7cd82504), .in143(32'h2c97e54e),
    .in144(32'h19eec0d9), .in145(32'h94c3f04f), .in146(32'h3e93f95c), .in147(32'h19c4802f),
    .in148(32'h5fa06c88), .in149(32'h626c80bf), .in150(32'hb2b917c9), .in151(32'h3bf07621),
    .in152(32'h850443aa), .in153(32'h96522919), .in154(32'hda91edf3), .in155(32'ha7da5f91),
    .in156(32'ha66cee82), .in157(32'hbc01523), .in158(32'h27394720), .in159(32'h1bb90743),
    .in160(32'h9ea2a65e), .in161(32'hd3119589), .in162(32'he934e2d), .in163(32'ha2c12e66),
    .in164(32'h849f4ea4), .in165(32'hbc3d2468), .in166(32'h4fc78859), .in167(32'h538a229b),
    .in168(32'h118c5f18), .in169(32'hbde471c3), .in170(32'h7b4cc38b), .in171(32'h5caed75d),
    .in172(32'h107f98d5), .in173(32'h19b1dad5), .in174(32'h3e5704d0), .in175(32'h429fee25),
    .in176(32'h40639707), .in177(32'h3c2fee7), .in178(32'he2e8b18d), .in179(32'h93589b43),
    .in180(32'h134545d3), .in181(32'h1a3fac58), .in182(32'h1572a724), .in183(32'h7bc89eb9),
    .in184(32'h31031dd2), .in185(32'ha22992e4), .in186(32'h8296e65e), .in187(32'h29978fab),
    .in188(32'h3f1df481), .in189(32'h5e761efb), .in190(32'h6320817b), .in191(32'hb9e95fad),
    .in192(32'hf6b93a23), .in193(32'hbc94d47a), .in194(32'h7e6d2053), .in195(32'h5df0f7fd),
    .in196(32'h33a301e6), .in197(32'h9deae4da), .in198(32'hc30b414c), .in199(32'h5d9454b5),
    .in200(32'h17f651e2), .in201(32'hd7f78fec), .in202(32'h8a37bf67), .in203(32'hcd8fad9),
    .in204(32'hd363bbf0), .in205(32'hb7a5618), .in206(32'hcc67cc08), .in207(32'h42912999),
    .in208(32'h77ec7e54), .in209(32'h1ff57825), .in210(32'h6fa1d4db), .in211(32'h8c9f89f6),
    .in212(32'hbb7c3f59), .in213(32'h3268dc64), .in214(32'heccf8223), .in215(32'h6cc275f5),
    .in216(32'hbc6aff74), .in217(32'hc27c178a), .in218(32'he0493c3), .in219(32'h50f413ab),
    .in220(32'h7cc52833), .in221(32'ha6b533b3), .in222(32'hb33be0ba), .in223(32'hffadf94b),
    .in224(32'h73f113c9), .in225(32'hbc33d241), .in226(32'hd7660e70), .in227(32'hfa04f0f6),
    .in228(32'hdd225f32), .in229(32'hc7bf9257), .in230(32'he18dd55), .in231(32'hadb2ad4),
    .in232(32'h45b0a00c), .in233(32'h2628e5cd), .in234(32'h9853acaf), .in235(32'h318164c4),
    .in236(32'h35a30d46), .in237(32'h7ebe3fcf), .in238(32'hc8ff19d9), .in239(32'h205e7034),
    .in240(32'h502a33e2), .in241(32'hb5b3e8a0), .in242(32'hc5957f6c), .in243(32'ha4323563),
    .in244(32'h79fe2ee4), .in245(32'h52038102), .in246(32'h76902cdc), .in247(32'hc8a36b27),
    .in248(32'h3b9b3e02), .in249(32'hc3e06a91), .in250(32'h8337afa8), .in251(32'hb6e5407f),
    .in252(32'h11ebdf22), .in253(32'h8706dfaa), .in254(32'h9e5e3db1), .in255(32'h18af3489), .out(result),
    .sel(in_data));
endmodule

module Multiplexer64 (
  input  [31:0] value_0,
  input  [31:0] value_1,
  input  [31:0] value_2,
  input  [31:0] value_3,
  input  [31:0] value_4,
  input  [31:0] value_5,
  input  [31:0] value_6,
  input  [31:0] value_7,
  input  [31:0] value_8,
  input  [31:0] value_9,
  input  [31:0] value_10,
  input  [31:0] value_11,
  input  [31:0] value_12,
  input  [31:0] value_13,
  input  [31:0] value_14,
  input  [31:0] value_15,
  input  [31:0] value_16,
  input  [31:0] value_17,
  input  [31:0] value_18,
  input  [31:0] value_19,
  input  [31:0] value_20,
  input  [31:0] value_21,
  input  [31:0] value_22,
  input  [31:0] value_23,
  input  [31:0] value_24,
  input  [31:0] value_25,
  input  [31:0] value_26,
  input  [31:0] value_27,
  input  [31:0] value_28,
  input  [31:0] value_29,
  input  [31:0] value_30,
  input  [31:0] value_31,
  input  [31:0] value_32,
  input  [31:0] value_33,
  input  [31:0] value_34,
  input  [31:0] value_35,
  input  [31:0] value_36,
  input  [31:0] value_37,
  input  [31:0] value_38,
  input  [31:0] value_39,
  input  [31:0] value_40,
  input  [31:0] value_41,
  input  [31:0] value_42,
  input  [31:0] value_43,
  input  [31:0] value_44,
  input  [31:0] value_45,
  input  [31:0] value_46,
  input  [31:0] value_47,
  input  [31:0] value_48,
  input  [31:0] value_49,
  input  [31:0] value_50,
  input  [31:0] value_51,
  input  [31:0] value_52,
  input  [31:0] value_53,
  input  [31:0] value_54,
  input  [31:0] value_55,
  input  [31:0] value_56,
  input  [31:0] value_57,
  input  [31:0] value_58,
  input  [31:0] value_59,
  input  [31:0] value_60,
  input  [31:0] value_61,
  input  [31:0] value_62,
  input  [31:0] value_63,
  input  [5:0] choice,
  output [31:0] out_66
);

  wire [31:0] and_1_out, and_2_out, bitextender1to32_1_result, multiplexer32_1_out_34,
       multiplexer32_2_out_34, not_1_out;

  Multiplexer32 multiplexer32_1 (
    .value_0(value_0), .value_1(value_1), .value_2(value_2), .value_3(value_3), .value_4(value_4),
    .value_5(value_5), .value_6(value_6), .value_7(value_7), .value_8(value_8), .value_9(value_9),
    .value_10(value_10), .value_11(value_11), .value_12(value_12), .value_13(value_13), .value_14(value_14),
    .value_15(value_15), .value_16(value_16), .value_17(value_17), .value_18(value_18), .value_19(value_19),
    .value_20(value_20), .value_21(value_21), .value_22(value_22), .value_23(value_23), .value_24(value_24),
    .value_25(value_25), .value_26(value_26), .value_27(value_27), .value_28(value_28), .value_29(value_29),
    .value_30(value_30), .value_31(value_31), .choice(choice[4:0]), .out_34(multiplexer32_1_out_34));
  Multiplexer32 multiplexer32_2 (
    .value_0(value_32), .value_1(value_33), .value_2(value_34), .value_3(value_35), .value_4(value_36),
    .value_5(value_37), .value_6(value_38), .value_7(value_39), .value_8(value_40), .value_9(value_41),
    .value_10(value_42), .value_11(value_43), .value_12(value_44), .value_13(value_45), .value_14(value_46),
    .value_15(value_47), .value_16(value_48), .value_17(value_49), .value_18(value_50), .value_19(value_51),
    .value_20(value_52), .value_21(value_53), .value_22(value_54), .value_23(value_55), .value_24(value_56),
    .value_25(value_57), .value_26(value_58), .value_27(value_59), .value_28(value_60), .value_29(value_61),
    .value_30(value_62), .value_31(value_63), .choice(choice[4:0]), .out_34(multiplexer32_2_out_34));
  BitExtender1To32 bitextender1to32_1 (.value(choice[5]), .result(bitextender1to32_1_result));
  assign and_1_out = multiplexer32_1_out_34 & not_1_out;  // AND_Gate and_1, 32 bits wide
  assign not_1_out = ~bitextender1to32_1_result;  // NOT_Gate not_1, 32 bits wide
  assign and_2_out = multiplexer32_2_out_34 & bitextender1to32_1_result;  // AND_Gate and_2, 32 bits wide
  assign out_66 = and_1_out | and_2_out;  // OR_Gate or_1, 32 bits wide
endmodule

module Multiplexer128 (
  input  [31:0] value_0,
  input  [31:0] value_1,
  input  [31:0] value_2,
  input  [31:0] value_3,
  input  [31:0] value_4,
  input  [31:0] value_5,
  input  [31:0] value_6,
  input  [31:0] value_7,
  input  [31:0] value_8,
  input  [31:0] value_9,
  input  [31:0] value_10,
  input  [31:0] value_11,
  input  [31:0] value_12,
  input  [31:0] value_13,
  input  [31:0] value_14,
  input  [31:0] value_15,
  input  [31:0] value_16,
  input  [31:0] value_17,
  input  [31:0] value_18,
  input  [31:0] value_19,
  input  [31:0] value_20,
  input  [31:0] value_21,
  input  [31:0] value_22,
  input  [31:0] value_23,
  input  [31:0] value_24,
  input  [31:0] value_25,
  input  [31:0] value_26,
  input  [31:0] value_27,
  input  [31:0] value_28,
  input  [31:0] value_29,
  input  [31:0] value_30,
  input  [31:0] value_31,
  input  [31:0] value_32,
  input  [31:0] value_33,
  input  [31:0] value_34,
  input  [31:0] value_35,
  input  [31:0] value_36,
  input  [31:0] value_37,
  input  [31:0] value_38,
  input  [31:0] value_39,
  input  [31:0] value_40,
  input  [31:0] value_41,
  input  [31:0] value_42,
  input  [31:0] value_43,
  input  [31:0] value_44,
  input  [31:0] value_45,
  input  [31:0] value_46,
  input  [31:0] value_47,
  input  [31:0] value_48,
  input  [31:0] value_49,
  input  [31:0] value_50,
  input  [31:0] value_51,
  input  [31:0] value_52,
  input  [31:0] value_53,
  input  [31:0] value_54,
  input  [31:0] value_55,
  input  [31:0] value_56,
  input  [31:0] value_57,
  input  [31:0] value_58,
  input  [31:0] value_59,
  input  [31:0] value_60,
  input  [31:0] value_61,
  input  [31:0] value_62,
  input  [31:0] value_63,
  input  [31:0] value_64,
  input  [31:0] value_65,
  input  [31:0] value_66,
  input  [31:0] value_67,
  input  [31:0] value_68,
  input  [31:0] value_69,
  input  [31:0] value_70,
  input  [31:0] value_71,
  input  [31:0] value_72,
  input  [31:0] value_73,
  input  [31:0] value_74,
  input  [31:0] value_75,
  input  [31:0] value_76,
  input  [31:0] value_77,
  input  [31:0] value_78,
  input  [31:0] value_79,
  input  [31:0] value_80,
  input  [31:0] value_81,
  input  [31:0] value_82,
  input  [31:0] value_83,
  input  [31:0] value_84,
  input  [31:0] value_85,
  input  [31:0] value_86,
  input  [31:0] value_87,
  input  [31:0] value_88,
  input  [31:0] value_89,
  input  [31:0] value_90,
  input  [31:0] value_91,
  input  [31:0] value_92,
  input  [31:0] value_93,
  input  [31:0] value_94,
  input  [31:0] value_95,
  input  [31:0] value_96,
  input  [31:0] value_97,
  input  [31:0] value_98,
  input  [31:0] value_99,
  input  [31:0] value_100,
  input  [31:0] value_101,
  input  [31:0] value_102,
  input  [31:0] value_103,
  input  [31:0] value_104,
  input  [31:0] value_105,
  input  [31:0] value_106,
  input  [31:0] value_107,
  input  [31:0] value_108,
  input  [31:0] value_109,
  input  [31:0] value_110,
  input  [31:0] value_111,
  input  [31:0] value_112,
  input  [31:0] value_113,
  input  [31:0] value_114,
  input  [31:0] value_115,
  input  [31:0] value_116,
  input  [31:0] value_117,
  input  [31:0] value_118,
  input  [31:0] value_119,
  input  [31:0] value_120,
  input  [31:0] value_121,
  input  [31:0] value_122,
  input  [31:0] value_123,
  input  [31:0] value_124,
  input  [31:0] value_125,
  input  [31:0] value_126,
  input  [31:0] value_127,
  input  [6:0] choice,
  output [31:0] out_130
);

  wire [31:0] and_1_out, and_2_out, bitextender1to32_1_result, multiplexer64_1_out_66,
       multiplexer64_2_out_66, not_1_out;

  Multiplexer64 multiplexer64_1 (
    .value_0(value_0), .value_1(value_1), .value_2(value_2), .value_3(value_3), .value_4(value_4),
    .value_5(value_5), .value_6(value_6), .value_7(value_7), .value_8(value_8), .value_9(value_9),
    .value_10(value_10), .value_11(value_11), .value_12(value_12), .value_13(value_13), .value_14(value_14),
    .value_15(value_15), .value_16(value_16), .value_17(value_17), .value_18(value_18), .value_19(value_19),
    .value_20(value_20), .value_21(value_21), .value_22(value_22), .value_23(value_23), .value_24(value_24),
    .value_25(value_25), .value_26(value_26), .value_27(value_27), .value_28(value_28), .value_29(value_29),
    .value_30(value_30), .value_31(value_31), .value_32(value_32), .value_33(value_33), .value_34(value_34),
    .value_35(value_35), .value_36(value_36), .value_37(value_37), .value_38(value_38), .value_39(value_39),
    .value_40(value_40), .value_41(value_41), .value_42(value_42), .value_43(value_43), .value_44(value_44),
    .value_45(value_45), .value_46(value_46), .value_47(value_47), .value_48(value_48), .value_49(value_49),
    .value_50(value_50), .value_51(value_51), .value_52(value_52), .value_53(value_53), .value_54(value_54),
    .value_55(value_55), .value_56(value_56), .value_57(value_57), .value_58(value_58), .value_59(value_59),
    .value_60(value_60), .value_61(value_61), .value_62(value_62), .value_63(value_63), .choice(choice[5:0]),
    .out_66(multiplexer64_1_out_66));
  Multiplexer64 multiplexer64_2 (
    .value_0(value_64), .value_1(value_65), .value_2(value_66), .value_3(value_67), .value_4(value_68),
    .value_5(value_69), .value_6(value_70), .value_7(value_71), .value_8(value_72), .value_9(value_73),
    .value_10(value_74), .value_11(value_75), .value_12(value_76), .value_13(value_77), .value_14(value_78),
    .value_15(value_79), .value_16(value_80), .value_17(value_81), .value_18(value_82), .value_19(value_83),
    .value_20(value_84), .value_21(value_85), .value_22(value_86), .value_23(value_87), .value_24(value_88),
    .value_25(value_89), .value_26(value_90), .value_27(value_91), .value_28(value_92), .value_29(value_93),
    .value_30(value_94), .value_31(value_95), .value_32(value_96), .value_33(value_97), .value_34(value_98),
    .value_35(value_99), .value_36(value_100), .value_37(value_101), .value_38(value_102),
    .value_39(value_103), .value_40(value_104), .value_41(value_105), .value_42(value_106),
    .value_43(value_107), .value_44(value_108), .value_45(value_109), .value_46(value_110),
    .value_47(value_111), .value_48(value_112), .value_49(value_113), .value_50(value_114),
    .value_51(value_115), .value_52(value_116), .value_53(value_117), .value_54(value_118),
    .value_55(value_119), .value_56(value_120), .value_57(value_121), .value_58(value_122),
    .value_59(value_123), .value_60(value_124), .value_61(value_125), .value_62(value_126),
    .value_63(value_127), .choice(choice[5:0]), .out_66(multiplexer64_2_out_66));
  BitExtender1To32 bitextender1to32_1 (.value(choice[6]), .result(bitextender1to32_1_result));
  assign and_1_out = multiplexer64_1_out_66 & not_1_out;  // AND_Gate and_1, 32 bits wide
  assign not_1_out = ~bitextender1to32_1_result;  // NOT_Gate not_1, 32 bits wide
  assign and_2_out = multiplexer64_2_out_66 & bitextender1to32_1_result;  // AND_Gate and_2, 32 bits wide
  assign out_130 = and_1_out | and_2_out;  // OR_Gate or_1, 32 bits wide
endmodule

module Multiplexer256 (
  input  [31:0] value_0,
  input  [31:0] value_1,
  input  [31:0] value_2,
  input  [31:0] value_3,
  input  [31:0] value_4,
  input  [31:0] value_5,
  input  [31:0] value_6,
  input  [31:0] value_7,
  input  [31:0] value_8,
  input  [31:0] value_9,
  input  [31:0] value_10,
  input  [31:0] value_11,
  input  [31:0] value_12,
  input  [31:0] value_13,
  input  [31:0] value_14,
  input  [31:0] value_15,
  input  [31:0] value_16,
  input  [31:0] value_17,
  input  [31:0] value_18,
  input  [31:0] value_19,
  input  [31:0] value_20,
  input  [31:0] value_21,
  input  [31:0] value_22,
  input  [31:0] value_23,
  input  [31:0] value_24,
  input  [31:0] value_25,
  input  [31:0] value_26,
  input  [31:0] value_27,
  input  [31:0] value_28,
  input  [31:0] value_29,
  input  [31:0] value_30,
  input  [31:0] value_31,
  input  [31:0] value_32,
  input  [31:0] value_33,
  input  [31:0] value_34,
  input  [31:0] value_35,
  input  [31:0] value_36,
  input  [31:0] value_37,
  input  [31:0] value_38,
  input  [31:0] value_39,
  input  [31:0] value_40,
  input  [31:0] value_41,
  input  [31:0] value_42,
  input  [31:0] value_43,
  input  [31:0] value_44,
  input  [31:0] value_45,
  input  [31:0] value_46,
  input  [31:0] value_47,
  input  [31:0] value_48,
  input  [31:0] value_49,
  input  [31:0] value_50,
  input  [31:0] value_51,
  input  [31:0] value_52,
  input  [31:0] value_53,
  input  [31:0] value_54,
  input  [31:0] value_55,
  input  [31:0] value_56,
  input  [31:0] value_57,
  input  [31:0] value_58,
  input  [31:0] value_59,
  input  [31:0] value_60,
  input  [31:0] value_61,
  input  [31:0] value_62,
  input  [31:0] value_63,
  input  [31:0] value_64,
  input  [31:0] value_65,
  input  [31:0] value_66,
  input  [31:0] value_67,
  input  [31:0] value_68,
  input  [31:0] value_69,
  input  [31:0] value_70,
  input  [31:0] value_71,
  input  [31:0] value_72,
  input  [31:0] value_73,
  input  [31:0] value_74,
  input  [31:0] value_75,
  input  [31:0] value_76,
  input  [31:0] value_77,
  input  [31:0] value_78,
  input  [31:0] value_79,
  input  [31:0] value_80,
  input  [31:0] value_81,
  input  [31:0] value_82,
  input  [31:0] value_83,
  input  [31:0] value_84,
  input  [31:0] value_85,
  input  [31:0] value_86,
  input  [31:0] value_87,
  input  [31:0] value_88,
  input  [31:0] value_89,
  input  [31:0] value_90,
  input  [31:0] value_91,
  input  [31:0] value_92,
  input  [31:0] value_93,
  input  [31:0] value_94,
  input  [31:0] value_95,
  input  [31:0] value_96,
  input  [31:0] value_97,
  input  [31:0] value_98,
  input  [31:0] value_99,
  input  [31:0] value_100,
  input  [31:0] value_101,
  input  [31:0] value_102,
  input  [31:0] value_103,
  input  [31:0] value_104,
  input  [31:0] value_105,
  input  [31:0] value_106,
  input  [31:0] value_107,
  input  [31:0] value_108,
  input  [31:0] value_109,
  input  [31:0] value_110,
  input  [31:0] value_111,
  input  [31:0] value_112,
  input  [31:0] value_113,
  input  [31:0] value_114,
  input  [31:0] value_115,
  input  [31:0] value_116,
  input  [31:0] value_117,
  input  [31:0] value_118,
  input  [31:0] value_119,
  input  [31:0] value_120,
  input  [31:0] value_121,
  input  [31:0] value_122,
  input  [31:0] value_123,
  input  [31:0] value_124,
  input  [31:0] value_125,
  input  [31:0] value_126,
  input  [31:0] value_127,
  input  [31:0] value_128,
  input  [31:0] value_129,
  input  [31:0] value_130,
  input  [31:0] value_131,
  input  [31:0] value_132,
  input  [31:0] value_133,
  input  [31:0] value_134,
  input  [31:0] value_135,
  input  [31:0] value_136,
  input  [31:0] value_137,
  input  [31:0] value_138,
  input  [31:0] value_139,
  input  [31:0] value_140,
  input  [31:0] value_141,
  input  [31:0] value_142,
  input  [31:0] value_143,
  input  [31:0] value_144,
  input  [31:0] value_145,
  input  [31:0] value_146,
  input  [31:0] value_147,
  input  [31:0] value_148,
  input  [31:0] value_149,
  input  [31:0] value_150,
  input  [31:0] value_151,
  input  [31:0] value_152,
  input  [31:0] value_153,
  input  [31:0] value_154,
  input  [31:0] value_155,
  input  [31:0] value_156,
  input  [31:0] value_157,
  input  [31:0] value_158,
  input  [31:0] value_159,
  input  [31:0] value_160,
  input  [31:0] value_161,
  input  [31:0] value_162,
  input  [31:0] value_163,
  input  [31:0] value_164,
  input  [31:0] value_165,
  input  [31:0] value_166,
  input  [31:0] value_167,
  input  [31:0] value_168,
  input  [31:0] value_169,
  input  [31:0] value_170,
  input  [31:0] value_171,
  input  [31:0] value_172,
  input  [31:0] value_173,
  input  [31:0] value_174,
  input  [31:0] value_175,
  input  [31:0] value_176,
  input  [31:0] value_177,
  input  [31:0] value_178,
  input  [31:0] value_179,
  input  [31:0] value_180,
  input  [31:0] value_181,
  input  [31:0] value_182,
  input  [31:0] value_183,
  input  [31:0] value_184,
  input  [31:0] value_185,
  input  [31:0] value_186,
  input  [31:0] value_187,
  input  [31:0] value_188,
  input  [31:0] value_189,
  input  [31:0] value_190,
  input  [31:0] value_191,
  input  [31:0] value_192,
  input  [31:0] value_193,
  input  [31:0] value_194,
  input  [31:0] value_195,
  input  [31:0] value_196,
  input  [31:0] value_197,
  input  [31:0] value_198,
  input  [31:0] value_199,
  input  [31:0] value_200,
  input  [31:0] value_201,
  input  [31:0] value_202,
  input  [31:0] value_203,
  input  [31:0] value_204,
  input  [31:0] value_205,
  input  [31:0] value_206,
  input  [31:0] value_207,
  input  [31:0] value_208,
  input  [31:0] value_209,
  input  [31:0] value_210,
  input  [31:0] value_211,
  input  [31:0] value_212,
  input  [31:0] value_213,
  input  [31:0] value_214,
  input  [31:0] value_215,
  input  [31:0] value_216,
  input  [31:0] value_217,
  input  [31:0] value_218,
  input  [31:0] value_219,
  input  [31:0] value_220,
  input  [31:0] value_221,
  input  [31:0] value_222,
  input  [31:0] value_223,
  input  [31:0] value_224,
  input  [31:0] value_225,
  input  [31:0] value_226,
  input  [31:0] value_227,
  input  [31:0] value_228,
  input  [31:0] value_229,
  input  [31:0] value_230,
  input  [31:0] value_231,
  input  [31:0] value_232,
  input  [31:0] value_233,
  input  [31:0] value_234,
  input  [31:0] value_235,
  input  [31:0] value_236,
  input  [31:0] value_237,
  input  [31:0] value_238,
  input  [31:0] value_239,
  input  [31:0] value_240,
  input  [31:0] value_241,
  input  [31:0] value_242,
  input  [31:0] value_243,
  input  [31:0] value_244,
  input  [31:0] value_245,
  input  [31:0] value_246,
  input  [31:0] value_247,
  input  [31:0] value_248,
  input  [31:0] value_249,
  input  [31:0] value_250,
  input  [31:0] value_251,
  input  [31:0] value_252,
  input  [31:0] value_253,
  input  [31:0] value_254,
  input  [31:0] value_255,
  input  [7:0] choice,
  output [31:0] out_258
);

  wire [31:0] and_1_out, and_2_out, bitextender1to32_1_result, multiplexer128_1_out_130,
       multiplexer128_2_out_130, not_1_out;

  Multiplexer128 multiplexer128_1 (
    .value_0(value_0), .value_1(value_1), .value_2(value_2), .value_3(value_3), .value_4(value_4),
    .value_5(value_5), .value_6(value_6), .value_7(value_7), .value_8(value_8), .value_9(value_9),
    .value_10(value_10), .value_11(value_11), .value_12(value_12), .value_13(value_13), .value_14(value_14),
    .value_15(value_15), .value_16(value_16), .value_17(value_17), .value_18(value_18), .value_19(value_19),
    .value_20(value_20), .value_21(value_21), .value_22(value_22), .value_23(value_23), .value_24(value_24),
    .value_25(value_25), .value_26(value_26), .value_27(value_27), .value_28(value_28), .value_29(value_29),
    .value_30(value_30), .value_31(value_31), .value_32(value_32), .value_33(value_33), .value_34(value_34),
    .value_35(value_35), .value_36(value_36), .value_37(value_37), .value_38(value_38), .value_39(value_39),
    .value_40(value_40), .value_41(value_41), .value_42(value_42), .value_43(value_43), .value_44(value_44),
    .value_45(value_45), .value_46(value_46), .value_47(value_47), .value_48(value_48), .value_49(value_49),
    .value_50(value_50), .value_51(value_51), .value_52(value_52), .value_53(value_53), .value_54(value_54),
    .value_55(value_55), .value_56(value_56), .value_57(value_57), .value_58(value_58), .value_59(value_59),
    .value_60(value_60), .value_61(value_61), .value_62(value_62), .value_63(value_63), .value_64(value_64),
    .value_65(value_65), .value_66(value_66), .value_67(value_67), .value_68(value_68), .value_69(value_69),
    .value_70(value_70), .value_71(value_71), .value_72(value_72), .value_73(value_73), .value_74(value_74),
    .value_75(value_75), .value_76(value_76), .value_77(value_77), .value_78(value_78), .value_79(value_79),
    .value_80(value_80), .value_81(value_81), .value_82(value_82), .value_83(value_83), .value_84(value_84),
    .value_85(value_85), .value_86(value_86), .value_87(value_87), .value_88(value_88), .value_89(value_89),
    .value_90(value_90), .value_91(value_91), .value_92(value_92), .value_93(value_93), .value_94(value_94),
    .value_95(value_95), .value_96(value_96), .value_97(value_97), .value_98(value_98), .value_99(value_99),
    .value_100(value_100), .value_101(value_101), .value_102(value_102), .value_103(value_103),
    .value_104(value_104), .value_105(value_105), .value_106(value_106), .value_107(value_107),
    .value_108(value_108), .value_109(value_109), .value_110(value_110), .value_111(value_111),
    .value_112(value_112), .value_113(value_113), .value_114(value_114), .value_115(value_115),
    .value_116(value_116), .value_117(value_117), .value_118(value_118), .value_119(value_119),
    .value_120(value_120), .value_121(value_121), .value_122(value_122), .value_123(value_123),
    .value_124(value_124), .value_125(value_125), .value_126(value_126), .value_127(value_127),
    .choice(choice[6:0]), .out_130(multiplexer128_1_out_130));
  Multiplexer128 multiplexer128_2 (
    .value_0(value_128), .value_1(value_129), .value_2(value_130), .value_3(value_131), .value_4(value_132),
    .value_5(value_133), .value_6(value_134), .value_7(value_135), .value_8(value_136), .value_9(value_137),
    .value_10(value_138), .value_11(value_139), .value_12(value_140), .value_13(value_141),
    .value_14(value_142), .value_15(value_143), .value_16(value_144), .value_17(value_145),
    .value_18(value_146), .value_19(value_147), .value_20(value_148), .value_21(value_149),
    .value_22(value_150), .value_23(value_151), .value_24(value_152), .value_25(value_153),
    .value_26(value_154), .value_27(value_155), .value_28(value_156), .value_29(value_157),
    .value_30(value_158), .value_31(value_159), .value_32(value_160), .value_33(value_161),
    .value_34(value_162), .value_35(value_163), .value_36(value_164), .value_37(value_165),
    .value_38(value_166), .value_39(value_167), .value_40(value_168), .value_41(value_169),
    .value_42(value_170), .value_43(value_171), .value_44(value_172), .value_45(value_173),
    .value_46(value_174), .value_47(value_175), .value_48(value_176), .value_49(value_177),
    .value_50(value_178), .value_51(value_179), .value_52(value_180), .value_53(value_181),
    .value_54(value_182), .value_55(value_183), .value_56(value_184), .value_57(value_185),
    .value_58(value_186), .value_59(value_187), .value_60(value_188), .value_61(value_189),
    .value_62(value_190), .value_63(value_191), .value_64(value_192), .value_65(value_193),
    .value_66(value_194), .value_67(value_195), .value_68(value_196), .value_69(value_197),
    .value_70(value_198), .value_71(value_199), .value_72(value_200), .value_73(value_201),
    .value_74(value_202), .value_75(value_203), .value_76(value_204), .value_77(value_205),
    .value_78(value_206), .value_79(value_207), .value_80(value_208), .value_81(value_209),
    .value_82(value_210), .value_83(value_211), .value_84(value_212), .value_85(value_213),
    .value_86(value_214), .value_87(value_215), .value_88(value_216), .value_89(value_217),
    .value_90(value_218), .value_91(value_219), .value_92(value_220), .value_93(value_221),
    .value_94(value_222), .value_95(value_223), .value_96(value_224), .value_97(value_225),
    .value_98(value_226), .value_99(value_227), .value_100(value_228), .value_101(value_229),
    .value_102(value_230), .value_103(value_231), .value_104(value_232), .value_105(value_233),
    .value_106(value_234), .value_107(value_235), .value_108(value_236), .value_109(value_237),
    .value_110(value_238), .value_111(value_239), .value_112(value_240), .value_113(value_241),
    .value_114(value_242), .value_115(value_243), .value_116(value_244), .value_117(value_245),
    .value_118(value_246), .value_119(value_247), .value_120(value_248), .value_121(value_249),
    .value_122(value_250), .value_123(value_251), .value_124(value_252), .value_125(value_253),
    .value_126(value_254), .value_127(value_255), .choice(choice[6:0]), .out_130(multiplexer128_2_out_130));
  BitExtender1To32 bitextender1to32_1 (.value(choice[7]), .result(bitextender1to32_1_result));
  assign and_1_out = multiplexer128_1_out_130 & not_1_out;  // AND_Gate and_1, 32 bits wide
  assign not_1_out = ~bitextender1to32_1_result;  // NOT_Gate not_1, 32 bits wide
  assign and_2_out = multiplexer128_2_out_130 & bitextender1to32_1_result;  // AND_Gate and_2, 32 bits wide
  assign out_258 = and_1_out | and_2_out;  // OR_Gate or_1, 32 bits wide
endmodule

module HalfAdder (
  input  value_0,
  input  value_1,
  output out_carry,
  output result
);

  and and_1 (out_carry, value_0, value_1);
  xor xor_1 (result, value_0, value_1);
endmodule

module FullAdder (
  input  value_0,
  input  value_1,
  input  in_carry,
  output out_carry,
  output result
);

  wire halfadder_1_out_carry, halfadder_1_result, halfadder_2_out_carry;

  HalfAdder halfadder_1 (
    .value_0(value_0), .value_1(value_1), .out_carry(halfadder_1_out_carry), .result(halfadder_1_result));
  HalfAdder halfadder_2 (
    .value_0(halfadder_1_result), .value_1(in_carry), .out_carry(halfadder_2_out_carry), .result(result));
  or or_1 (out_carry, halfadder_1_out_carry, halfadder_2_out_carry);
endmodule

module Adder32Bits (
  input  [31:0] value_0,
  input  [31:0] value_1,
  input  in_carry,
  output out_carry,
  output [31:0] result
);

  wire adder16bits_1_out_carry;

  Adder16Bits adder16bits_1 (
    .value_0(value_0[15:0]), .value_1(value_1[15:0]), .in_carry(in_carry),
    .out_carry(adder16bits_1_out_carry), .result(result[15:0]));
  Adder16Bits adder16bits_2 (
    .value_0(value_0[31:16]), .value_1(value_1[31:16]), .in_carry(adder16bits_1_out_carry),
    .out_carry(out_carry), .result(result[31:16]));
  FullAdder fulladder_1 ();  // open: value_0, value_1, in_carry, out_carry, result
endmodule

module Adder2Bits (
  input  [1:0] value_0,
  input  [1:0] value_1,
  input  in_carry,
  output out_carry,
  output [1:0] result
);

  wire fulladder_1_out_carry;

  FullAdder fulladder_1 (
    .value_0(value_0[0]), .value_1(value_1[0]), .in_carry(in_carry), .out_carry(fulladder_1_out_carry),
    .result(result[0]));
  FullAdder fulladder_2 (
    .value_0(value_0[1]), .value_1(value_1[1]), .in_carry(fulladder_1_out_carry), .out_carry(out_carry),
    .result(result[1]));
  FullAdder fulladder_3 ();  // open: value_0, value_1, in_carry, out_carry, result
endmodule

module Adder4Bits (
  input  [3:0] value_0,
  input  [3:0] value_1,
  input  in_carry,
  output out_carry,
  output [3:0] result
);

  wire adder2bits_1_out_carry;

  Adder2Bits adder2bits_1 (
    .value_0(value_0[1:0]), .value_1(value_1[1:0]), .in_carry(in_carry), .out_carry(adder2bits_1_out_carry),
    .result(result[1:0]));
  Adder2Bits adder2bits_2 (
    .value_0(value_0[3:2]), .value_1(value_1[3:2]), .in_carry(adder2bits_1_out_carry), .out_carry(out_carry),
    .result(result[3:2]));
  FullAdder fulladder_1 ();  // open: value_0, value_1, in_carry, out_carry, result
endmodule

module Adder8Bits (
  input  [7:0] value_0,
  input  [7:0] value_1,
  input  in_carry,
  output out_carry,
  output [7:0] result
);

  wire adder4bits_1_out_carry;

  Adder4Bits adder4bits_1 (
    .value_0(value_0[3:0]), .value_1(value_1[3:0]), .in_carry(in_carry), .out_carry(adder4bits_1_out_carry),
    .result(result[3:0]));
  Adder4Bits adder4bits_2 (
    .value_0(value_0[7:4]), .value_1(value_1[7:4]), .in_carry(adder4bits_1_out_carry), .out_carry(out_carry),
    .result(result[7:4]));
  FullAdder fulladder_1 ();  // open: value_0, value_1, in_carry, out_carry, result
endmodule

module Adder16Bits (
  input  [15:0] value_0,
  input  [15:0] value_1,
  input  in_carry,
  output out_carry,
  output [15:0] result
);

  wire adder8bits_1_out_carry;

  Adder8Bits adder8bits_1 (
    .value_0(value_0[7:0]), .value_1(value_1[7:0]), .in_carry(in_carry), .out_carry(adder8bits_1_out_carry),
    .result(result[7:0]));
  Adder8Bits adder8bits_2 (
    .value_0(value_0[15:8]), .value_1(value_1[15:8]), .in_carry(adder8bits_1_out_carry),
    .out_carry(out_carry), .result(result[15:8]));
  FullAdder fulladder_1 ();  // open: value_0, value_1, in_carry, out_carry, result
endmodule

module Adder (
  input  [31:0] value_0,
  input  [31:0] value_1,
  output [31:0] result
);

  Adder32Bits adder32bits_1 (
    .value_0(value_0), .value_1(value_1), .in_carry(1'b0), .result(result));  // open: out_carry
endmodule

module Iteration (
  input  [31:0] value_0,
  input  [31:0] value_1,
  input  [4:0] index,
  input  inverse,
  output [31:0] result_0,
  output [31:0] result_1
);

  wire [31:0] ffunction_1_out_2, pblocks_1_out_3;

  PBlocks pblocks_1 (.index(index), .inverse(inverse), .out_3(pblocks_1_out_3));
  assign result_0 = value_1 ^ pblocks_1_out_3;  // XOR_Gate xor_1, 32 bits wide
  assign result_1 = value_0 ^ ffunction_1_out_2;  // XOR_Gate xor_2, 32 bits wide
  FFunction ffunction_1 (.value(result_0), .out_2(ffunction_1_out_2));
endmodule

module PBlocks (
  input  [4:0] index,
  input  inverse,
  output [31:0] out_3
);

  wire not_1_out;
  wire [31:0] multiplexer_1_out, multiplexer_2_out;

  not not_1 (not_1_out, inverse);
  Multiplexer #(.enable("true"), .select(5), .width(32)) multiplexer_1 (
    .in0(32'hb8fbc8db), .in1(32'hb0168b9a), .in2(32'h803570fd), .in3(32'h7a90b62f), .in4(32'ha6c0a9a7),
    .in5(32'h92672e9c), .in6(32'h2a72f6d3), .in7(32'h69bd26b), .in8(32'he95144e2), .in9(32'he479ed73),
    .in10(32'h1ee32253), .in11(32'h485ea77d), .in12(32'hba088783), .in13(32'h79c13872), .in14(32'hc92a6921),
    .in15(32'h37dc6cc8), .in16(32'hd3d887c0), .in17(32'h56bf40b), .out(multiplexer_1_out), .sel(index),
    .en(not_1_out));  // open: in18, in19, in20, in21, in22, in23, in24, in25, in26, in27, in28, in29, in30, in31
  assign out_3 = multiplexer_1_out | multiplexer_2_out;  // OR_Gate or_1, 32 bits wide
  Multiplexer #(.enable("true"), .select(5), .width(32)) multiplexer_2 (
    .in0(32'h56bf40b), .in1(32'hd3d887c0), .in2(32'h37dc6cc8), .in3(32'hc92a6921), .in4(32'h79c13872),
    .in5(32'hba088783), .in6(32'h485ea77d), .in7(32'h1ee32253), .in8(32'he479ed73), .in9(32'he95144e2),
    .in10(32'h69bd26b), .in11(32'h2a72f6d3), .in12(32'h92672e9c), .in13(32'ha6c0a9a7), .in14(32'h7a90b62f),
    .in15(32'h803570fd), .in16(32'hb0168b9a), .in17(32'hb8fbc8db), .out(multiplexer_2_out), .sel(index),
    .en(inverse));  // open: in18, in19, in20, in21, in22, in23, in24, in25, in26, in27, in28, in29, in30, in31
endmodule
