// Logisim project blowfish.circ as structural Verilog: 2 circuits, main circuit main
module main (
  input  enable,
  input  [63:0] in_data,
  input  [63:0] key,
  input  mode,
  output [63:0] out_data
);

  BlowfishCodec blowfishcodec_1 (.enable(enable), .in_data(in_data), .key(key), .mode(mode), .out_data(out_data));
endmodule

module BlowfishCodec (
  input  enable,
  input  [63:0] in_data,
  input  [63:0] key,
  input  mode,
  output [63:0] out_data
);
endmodule
